# Fritzing sketch Sensor_Array (saved by Fritzing 0.9.3b)
circuit board: 4.14787cm x 2.90303cm
stripboards: 1

parts:
  J-S1 = male pin header, 3 pins [form="♂ (male)"]
  J-S2 = male pin header, 3 pins [form="♂ (male)"]
  J-S4 = male pin header, 3 pins [form="♂ (male)"]
  J-S5 = male pin header, 3 pins [form="♂ (male)"]
  J-Power = male pin header, 3 pins [form="♂ (male)"]
  J-Out = male pin header, 5 pins [form="♂ (male)"]
  Arduino = Arduino Uno (Rev3)
  Q2 = NPN-Transistor [package="TO92 [THT]"]
  Sensor_1 = Soil Moisture Sensor
  Sensor_2 = Soil Moisture Sensor
  Sensor_3 = Soil Moisture Sensor
  Sensor_4 = Soil Moisture Sensor
  Sensor_5 = Soil Moisture Sensor
  J-S3 = male pin header, 3 pins [form="♂ (male)"]

nets:
  VCC: J-S1.pin1, J-S2.pin1, J-S4.pin1, J-S5.pin1, Q2.E, Sensor_1.VCC, Sensor_2.VCC, Sensor_3.VCC, Sensor_4.VCC, Sensor_5.VCC, J-S3.pin1
  GND: J-S1.pin2, J-S2.pin2, J-S4.pin2, J-S5.pin2, J-Power.pin3, Arduino.GND, Sensor_1.GND, Sensor_2.GND, Sensor_3.GND, Sensor_4.GND, Sensor_5.GND, J-S3.pin2
  N1: J-S1.pin3, J-Out.pin1, Arduino.A0, Sensor_1.SIG
  N2: J-S2.pin3, J-Out.pin2, Arduino.A1, Sensor_2.SIG
  N3: J-S4.pin3, J-Out.pin4, Arduino.A3, Sensor_4.SIG
  N4: J-S5.pin3, J-Out.pin5, Arduino.A4/SDA, Sensor_5.SIG
  N5: J-Power.pin1, Arduino.D7, Q2.B
  N6: J-Power.pin2, Arduino.5V, Q2.C
  N7: J-Out.pin3, Arduino.A2, Sensor_3.SIG, J-S3.pin3

notes:
  GND
  VCC
  SIG
  S-O5
  S-O4
  S-O3
  S-O2
  S-O1
